# Fritzing sketch omega_lora_dht11 (saved by Fritzing 0.9.3b)
breadboards: 1

parts:
  U1 = Onion Omega2 and Expansion Dock
  part = Adafruit RFM9x LoRa Radio [part_number=IC2]
  IC3 = DHT11 Humitidy and Temperature Sensor
  IC1 = SSOP16 [chip_label=SC18IS602B package=SSOP]
  ANT1 = Antenna
  R1 = Resistor [tolerance=±5% resistance=10k package=THT]

nets (from the breadboard view):
  N1: U1.GPIO18, IC3.DATA, R1.Pin_1
  N2: U1.SCL, IC1.8
  N3: U1.GPIO1, part.DIO1
  N4: U1.SDA, IC1.7
  N5: U1.GPIO0, part.DIO0
  GND: U1.GND, part.GND, IC3.GND, IC1.4, IC1.14, IC1.15, IC1.16
  3.3V: U1.3.3V, part.VIN, IC3.VDD, IC1.12, R1.Pin_0
  N6: part.ANTENNA, ANT1.antenna_lead
  N7: part.SCK, IC1.11
  N8: part.MISO, IC1.5
  N9: part.MOSI, IC1.6
  N10: part.CS, IC1.1

custom parts:
  Onion Omega2 and Expansion Dock: Onion Omega2 IoT Computer on Expansion Dock Omega2: - 580 Mhz MIPS CPU - 64MB RAM, Omega2+: 128MB RAM - 16MB Flash, Omega2+: 32M Flash - LEDE Linux OS - USB2.0 - 2.4GHz b/g/n WiFi - 15GPIO - 2PWM - 2 UART - 1 I2C - 1 SPI - 1 I2S - Micro-SD Card Slot (Omega2+ only) Expansion Dock: - Micro USB Port: Power and USB-to-Serial - USB Type-A Host Port - Reset Button - Power Switch - RGB LED -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
  Adafruit RFM9x LoRa Radio: Sending data over long distances is like magic, and now you can be a magician with this range of powerful and easy-to-use radio modules. Sure, sometimes you want to talk to a computer (a good time to use WiFi) or perhaps communicate with a Phone (choose Bluetooth Low Energy!) but what if you want to send data very far? Most WiFi, Bluetooth, Zigbee and other wireless chipsets use 2.4GHz, which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
  DHT11 Humitidy and Temperature Sensor: DHT11 Humidity and Temperature Sensor
